// Logisim project r162.circ as structural Verilog: 10 circuits, main circuit main
module main (
);

  wire adder_1_cout, adder_2_cout, and_1_out, and_2_out, and_3_out, and_4_out, and_5_out, and_6_out,
       and_7_out, clock_1_out, control_1_branch, control_1_jump, control_1_memread, control_1_memwrite,
       control_1_regtoa, control_1_regtob, dipswitch_1_sw1, ex_me_psb_1_memread, ex_me_psb_1_memwrite,
       forwardunit_1_afromme, forwardunit_1_afromwb, forwardunit_1_bfromme, forwardunit_1_bfromwb,
       forwardunit_1_storefromme, forwardunit_1_storefromwb, hazarddetector_1_stall, id_ex_psb_1_branch,
       id_ex_psb_1_branchtype, id_ex_psb_1_jump, id_ex_psb_1_memread, id_ex_psb_1_memwrite,
       id_ex_psb_1_regtoa, id_ex_psb_1_regtob, me_wb_psb_1_memread, not_1_out, not_2_out, not_3_out,
       or_1_out, or_2_out, or_3_out, or_4_out, xor_1_out;
  wire [3:0] control_1_aluop, control_1_busb, control_1_writebackdst, ex_me_psb_1_writebackdst,
       id_ex_psb_1_aluop, id_ex_psb_1_memwritereg, id_ex_psb_1_rega, id_ex_psb_1_regb,
       id_ex_psb_1_writebackdst, if_id_psb_1_instruction, if_id_psb_1_instruction_3,
       me_wb_psb_1_writebackdst, multiplexer_3_out, multiplexer_7_out;
  wire [7:0] if_id_psb_1_instruction_2;
  wire [15:0] adder_1_out, adder_2_out, alu_1_result, bit_extender_1_out, control_1_busa,
       ex_me_psb_1_aluresult, ex_me_psb_1_memwriteval, ex_me_psb_1_writebackval, id_ex_psb_1_busa,
       id_ex_psb_1_busb, id_ex_psb_1_jumppc, id_ex_psb_1_memwriteval, id_ex_psb_1_nextpc, if_id_psb_1_nextpc,
       me_wb_psb_1_memreadval, me_wb_psb_1_writebackval, multiplexer_1_out, multiplexer_2_out,
       multiplexer_4_out, multiplexer_5_out, multiplexer_6_out, multiplexer_8_out, multiplexer_9_out,
       multiplexer_10_out, multiplexer_11_out, multiplexer_12_out, multiplexer_13_out, multiplexer_14_out,
       multiplexer_15_out, multiplexer_16_out, multiplexer_17_out, PC_q, ram_1_dout, registerfile_1_outputa,
       registerfile_1_outputb, rom_1_data;
  wire [15:4] control_1_busb_2;

  ROM #(.addrWidth(16), .dataWidth(16)) rom_1 (.addr(PC_q), .data(rom_1_data));
  Register #(.width(16)) PC (.D(multiplexer_1_out), .en(not_2_out), .clk(clock_1_out), .Q(PC_q), .clr(dipswitch_1_sw1));
  // NoConnect on adder_1_cout
  Multiplexer #(.width(16)) multiplexer_1 (
    .in0(adder_1_out), .in1(multiplexer_8_out), .out(multiplexer_1_out), .sel(or_1_out));
  Adder #(.width(16)) adder_1 (.a(PC_q), .b(16'h1), .out(adder_1_out), .cin(1'b0), .cout(adder_1_cout));
  Multiplexer #(.width(16)) multiplexer_2 (.in0(rom_1_data), .in1({16{1'b0}}), .out(multiplexer_2_out), .sel(or_1_out));
  DipSwitch #(.number(1)) dipswitch_1 (.sw1(dipswitch_1_sw1));
  Clock clock_1 (.out(clock_1_out));
  IF_ID_PSB if_id_psb_1 (
    .inextPC(adder_1_out), .iinstruction(multiplexer_2_out), .writeEnable(not_2_out), .clock(clock_1_out),
    .reset(dipswitch_1_sw1), .nextPC(if_id_psb_1_nextpc),
    .instruction({if_id_psb_1_instruction_3, if_id_psb_1_instruction_2, if_id_psb_1_instruction}));
  // Probe on multiplexer_17_out
  // Probe on me_wb_psb_1_writebackdst
  Control control_1 (
    .instruction({if_id_psb_1_instruction_3, if_id_psb_1_instruction_2, if_id_psb_1_instruction}),
    .busA(control_1_busa), .regToA(control_1_regtoa), .busB({control_1_busb_2, control_1_busb}),
    .regToB(control_1_regtob), .aluOp(control_1_aluop), .writebackDst(control_1_writebackdst),
    .memWrite(control_1_memwrite), .memRead(control_1_memread), .branch(control_1_branch),
    .jump(control_1_jump));
  Multiplexer #(.width(4)) multiplexer_3 (
    .in0(control_1_busa[3:0]), .in1(if_id_psb_1_instruction_3), .out(multiplexer_3_out),
    .sel(control_1_memwrite));
  or or_1 (or_1_out, and_5_out, or_3_out);
  assign bit_extender_1_out = {{8{if_id_psb_1_instruction_2[7]}}, if_id_psb_1_instruction_2};  // Bit_Extender bit_extender_1
  Multiplexer #(.width(16)) multiplexer_4 (
    .in0(bit_extender_1_out), .in1({control_1_busb_2, control_1_busb}), .out(multiplexer_4_out),
    .sel(control_1_jump));
  RegisterFile registerfile_1 (
    .selectA(multiplexer_3_out), .selectB(control_1_busb), .selectWrite(me_wb_psb_1_writebackdst),
    .write(multiplexer_17_out), .clock(clock_1_out), .reset(dipswitch_1_sw1),
    .outputA(registerfile_1_outputa), .outputB(registerfile_1_outputb));
  Adder #(.width(16)) adder_2 (
    .a(if_id_psb_1_nextpc), .b(multiplexer_4_out), .out(adder_2_out), .cin(1'b0), .cout(adder_2_cout));
  // NoConnect on adder_2_cout
  not not_1 (not_1_out, or_2_out);
  or or_2 (or_2_out, or_3_out, hazarddetector_1_stall);
  HazardDetector hazarddetector_1 (
    .EXwritebackDst(id_ex_psb_1_writebackdst), .EXmemRead(id_ex_psb_1_memread), .IDregA(multiplexer_3_out),
    .IDregToA(control_1_regtoa), .IDregB(control_1_busb), .IDregToB(control_1_regtob),
    .stall(hazarddetector_1_stall));
  not not_2 (not_2_out, hazarddetector_1_stall);
  Multiplexer #(.width(16)) multiplexer_5 (
    .in0(control_1_busa), .in1(registerfile_1_outputa), .out(multiplexer_5_out), .sel(control_1_regtoa));
  Multiplexer #(.width(16)) multiplexer_6 (
    .in0({control_1_busb_2, control_1_busb}), .in1(registerfile_1_outputb), .out(multiplexer_6_out),
    .sel(control_1_regtob));
  Multiplexer #(.width(4)) multiplexer_7 (
    .in0(control_1_writebackdst), .in1(4'b0000), .out(multiplexer_7_out), .sel(or_2_out));
  Multiplexer #(.width(16)) multiplexer_8 (
    .in0(adder_2_out), .in1(multiplexer_9_out), .out(multiplexer_8_out), .sel(or_3_out));
  and and_1 (and_1_out, not_1_out, control_1_memwrite);
  and and_2 (and_2_out, not_1_out, control_1_memread);
  and and_3 (and_3_out, not_1_out, control_1_branch);
  and and_4 (and_4_out, not_1_out, control_1_jump);
  and and_5 (and_5_out, and_4_out, not_3_out);
  Multiplexer #(.width(16)) multiplexer_9 (
    .in0(id_ex_psb_1_jumppc), .in1(multiplexer_14_out), .out(multiplexer_9_out), .sel(and_7_out));
  not not_3 (not_3_out, control_1_regtob);
  or or_3 (or_3_out, and_6_out, and_7_out);
  xor xor_1 (xor_1_out, or_4_out, id_ex_psb_1_branchtype);
  and and_6 (and_6_out, xor_1_out, id_ex_psb_1_branch);
  // Probe on multiplexer_11_out
  // Probe on multiplexer_14_out
  ID_EX_PSB id_ex_psb_1 (
    .ibusA(multiplexer_5_out), .ibusB(multiplexer_6_out), .ialuOp(control_1_aluop), .imemRead(and_2_out),
    .imemWrite(and_1_out), .imemWriteVal(registerfile_1_outputa), .inextPC(if_id_psb_1_nextpc),
    .ijumpPC(adder_2_out), .ijump(and_4_out), .ibranch(and_3_out), .ibranchType(if_id_psb_1_instruction[2]),
    .iwritebackDst(multiplexer_7_out), .iregA(multiplexer_3_out), .iregToA(control_1_regtoa),
    .iregB(control_1_busb), .iregToB(control_1_regtob), .imemWriteReg(if_id_psb_1_instruction_3),
    .writeEnable(1'b1), .clock(clock_1_out), .reset(dipswitch_1_sw1), .busA(id_ex_psb_1_busa),
    .busB(id_ex_psb_1_busb), .aluOp(id_ex_psb_1_aluop), .memRead(id_ex_psb_1_memread),
    .memWrite(id_ex_psb_1_memwrite), .memWriteVal(id_ex_psb_1_memwriteval), .nextPC(id_ex_psb_1_nextpc),
    .jumpPC(id_ex_psb_1_jumppc), .jump(id_ex_psb_1_jump), .branch(id_ex_psb_1_branch),
    .branchType(id_ex_psb_1_branchtype), .writebackDst(id_ex_psb_1_writebackdst), .regA(id_ex_psb_1_rega),
    .regToA(id_ex_psb_1_regtoa), .regB(id_ex_psb_1_regb), .regToB(id_ex_psb_1_regtob),
    .memWriteReg(id_ex_psb_1_memwritereg));
  and and_7 (and_7_out, id_ex_psb_1_jump, id_ex_psb_1_regtob);
  or or_4 (or_4_out, multiplexer_11_out[0], multiplexer_11_out[1], multiplexer_11_out[2], multiplexer_11_out[3], multiplexer_11_out[4], multiplexer_11_out[5], multiplexer_11_out[6], multiplexer_11_out[7], multiplexer_11_out[9], multiplexer_11_out[10], multiplexer_11_out[11], multiplexer_11_out[12], multiplexer_11_out[13], multiplexer_11_out[14], multiplexer_11_out[15], multiplexer_11_out[8]);
  ForwardUnit forwardunit_1 (
    .MEdst(ex_me_psb_1_writebackdst), .WBdst(me_wb_psb_1_writebackdst), .r1(id_ex_psb_1_rega),
    .r1a(id_ex_psb_1_regtoa), .r2(id_ex_psb_1_regb), .r2a(id_ex_psb_1_regtob),
    .rStore(id_ex_psb_1_memwritereg), .rStorea(id_ex_psb_1_memwrite), .aFromME(forwardunit_1_afromme),
    .aFromWB(forwardunit_1_afromwb), .bFromME(forwardunit_1_bfromme), .bFromWB(forwardunit_1_bfromwb),
    .storeFromME(forwardunit_1_storefromme), .storeFromWB(forwardunit_1_storefromwb));
  ALU alu_1 (
    .A(multiplexer_11_out), .B(multiplexer_14_out), .operation(id_ex_psb_1_aluop), .result(alu_1_result));  // open: zero
  Multiplexer #(.width(16)) multiplexer_10 (
    .in0(id_ex_psb_1_busa), .in1(multiplexer_17_out), .out(multiplexer_10_out), .sel(forwardunit_1_afromwb));
  Multiplexer #(.width(16)) multiplexer_11 (
    .in0(multiplexer_10_out), .in1(ex_me_psb_1_writebackval), .out(multiplexer_11_out),
    .sel(forwardunit_1_afromme));
  Multiplexer #(.width(16)) multiplexer_12 (
    .in0(alu_1_result), .in1(id_ex_psb_1_nextpc), .out(multiplexer_12_out), .sel(id_ex_psb_1_jump));
  Multiplexer #(.width(16)) multiplexer_13 (
    .in0(id_ex_psb_1_busb), .in1(multiplexer_17_out), .out(multiplexer_13_out), .sel(forwardunit_1_bfromwb));
  Multiplexer #(.width(16)) multiplexer_14 (
    .in0(multiplexer_13_out), .in1(ex_me_psb_1_writebackval), .out(multiplexer_14_out),
    .sel(forwardunit_1_bfromme));
  Multiplexer #(.width(16)) multiplexer_15 (
    .in0(id_ex_psb_1_memwriteval), .out(multiplexer_15_out), .sel(forwardunit_1_storefromwb));  // open: in1
  Multiplexer #(.width(16)) multiplexer_16 (
    .in0(multiplexer_15_out), .in1(ex_me_psb_1_writebackval), .out(multiplexer_16_out),
    .sel(forwardunit_1_storefromme));
  // Probe on alu_1_result
  // Probe on ex_me_psb_1_aluresult
  EX_ME_PSB ex_me_psb_1 (
    .iwritebackVal(multiplexer_12_out), .ialuResult(alu_1_result), .imemRead(id_ex_psb_1_memread),
    .imemWrite(id_ex_psb_1_memwrite), .imemWriteVal(multiplexer_16_out),
    .iwritebackDst(id_ex_psb_1_writebackdst), .writeEnable(1'b1), .clock(clock_1_out),
    .reset(dipswitch_1_sw1), .writebackVal(ex_me_psb_1_writebackval), .aluResult(ex_me_psb_1_aluresult),
    .memRead(ex_me_psb_1_memread), .memWrite(ex_me_psb_1_memwrite), .memWriteVal(ex_me_psb_1_memwriteval),
    .writebackDst(ex_me_psb_1_writebackdst));
  RAM #(.addrWidth(16), .dataWidth(16)) ram_1 (
    .addr(ex_me_psb_1_aluresult), .we(ex_me_psb_1_memwrite), .oe(ex_me_psb_1_memread), .clk(clock_1_out),
    .din(ex_me_psb_1_memwriteval), .dout(ram_1_dout));
  ME_WB_PSB me_wb_psb_1 (
    .iwritebackVal(ex_me_psb_1_writebackval), .imemReadVal(ram_1_dout), .imemRead(ex_me_psb_1_memread),
    .iwritebackDst(ex_me_psb_1_writebackdst), .writeEnable(1'b1), .clock(clock_1_out),
    .reset(dipswitch_1_sw1), .writebackVal(me_wb_psb_1_writebackval), .memReadVal(me_wb_psb_1_memreadval),
    .memRead(me_wb_psb_1_memread), .writebackDst(me_wb_psb_1_writebackdst));
  Multiplexer #(.width(16)) multiplexer_17 (
    .in0(me_wb_psb_1_writebackval), .in1(me_wb_psb_1_memreadval), .out(multiplexer_17_out),
    .sel(me_wb_psb_1_memread));

  // Notes on the sheet:
  //   contents of rom_1 (hex, n*v repeats v):
  //   1005 2015 40a5 3212 1022 2032 4ff9 4fb8 2010 ffff
  //   TODO: have jal/jalr place the next PC on bus A instead of a specific bus
endmodule

module Control (
  input  [15:0] instruction,
  output [15:0] busA,
  output regToA,
  output [15:0] busB,
  output regToB,
  output [3:0] aluOp,
  output [3:0] writebackDst,
  output memWrite,
  output memRead,
  output branch,
  output jump
);

  wire ADDI_out, and_1_out, and_2_out, and_3_out, and_4_out, and_5_out, can_simplify_with_a34_out,
       can_simplify_with_b23_out, DIV_out, I_out, J_out, JALR_out, LI_out, LS_out, not_1_out, not_2_out,
       not_3_out, not_4_out, not_5_out, not_6_out, not_7_out, not_8_out, not_9_out, not_10_out, not_13_out,
       not_14_out, or_1_out, or_2_out, or_3_out, or_4_out, R_out, S_OTHER_out, S_out, SI_out, SR_out,
       UNNECESSARY_out;
  wire [15:0] bit_extender_1_out, bit_extender_2_out, dipswitch_1_sw16;

  DipSwitch #(.number(16)) dipswitch_1 (
    .sw1(dipswitch_1_sw16[15]), .sw2(dipswitch_1_sw16[14]), .sw3(dipswitch_1_sw16[13]),
    .sw4(dipswitch_1_sw16[12]), .sw5(dipswitch_1_sw16[11]), .sw6(dipswitch_1_sw16[10]),
    .sw7(dipswitch_1_sw16[9]), .sw8(dipswitch_1_sw16[8]), .sw9(dipswitch_1_sw16[7]),
    .sw10(dipswitch_1_sw16[6]), .sw11(dipswitch_1_sw16[5]), .sw12(dipswitch_1_sw16[4]),
    .sw13(dipswitch_1_sw16[3]), .sw14(dipswitch_1_sw16[2]), .sw15(dipswitch_1_sw16[1]),
    .sw16(dipswitch_1_sw16[0]));
  and and_1 (and_1_out, and_2_out, instruction[5]);
  not not_1 (not_1_out, and_2_out);
  and and_2 (and_2_out, instruction[7], instruction[6]);
  and and_3 (and_3_out, not_1_out, instruction[5]);
  not not_2 (not_2_out, instruction[3]);
  and and_4 (and_4_out, not_3_out, not_4_out);
  not not_3 (not_3_out, instruction[1]);
  and I (I_out, not_3_out, instruction[0]);
  and R (R_out, instruction[1], not_4_out);
  not not_4 (not_4_out, instruction[0]);
  and J (J_out, instruction[1], instruction[0]);
  not not_5 (not_5_out, instruction[2]);
  not not_6 (not_6_out, instruction[4]);
  and and_5 (and_5_out, not_2_out, and_4_out);
  and B (branch, instruction[3], and_4_out);
  not not_7 (not_7_out, and_1_out);
  and S_OTHER (S_OTHER_out, not_7_out, S_out);
  and DIV (DIV_out, not_5_out, and_1_out, S_out);
  and JALR (JALR_out, instruction[2], and_1_out, S_out);
  // NoConnect on SR_out
  not not_8 (not_8_out, and_3_out);
  and SR (SR_out, not_8_out, S_out);
  and SI (SI_out, and_3_out, S_out);
  and S (S_out, not_6_out, and_5_out);
  and LS (LS_out, instruction[4], and_5_out);
  not not_9 (not_9_out, instruction[2]);
  and LI (LI_out, instruction[2], I_out);
  and ADDI (ADDI_out, I_out, not_9_out);
  assign aluOp = S_OTHER_out ? {1'b1, instruction[7:6], instruction[2]} : 4'bz;  // Controlled_Buffer controlled_buffer_1
  assign aluOp = DIV_out ? 4'b0100 : 4'bz;  // Controlled_Buffer OP_DIV
  or can_simplify_with_a34 (can_simplify_with_a34_out, JALR_out, LS_out, I_out, J_out);
  assign aluOp = can_simplify_with_a34_out ? 4'b0000 : 4'bz;  // Controlled_Buffer OP_ADD
  assign aluOp = branch ? 4'b0001 : 4'bz;  // Controlled_Buffer OP_SUB
  assign aluOp = R_out ? {2'b00, instruction[3:2]} : 4'bz;  // Controlled_Buffer controlled_buffer_2
  assign busA = LS_out ? {{13{1'b0}}, instruction[7:5]} : 16'bz;  // Controlled_Buffer controlled_buffer_3
  assign busA = or_1_out ? {{12{1'b0}}, instruction[15:12]} : 16'bz;  // Controlled_Buffer controlled_buffer_4
  or or_1 (or_1_out, S_out, ADDI_out, branch);
  assign busA = R_out ? {{12{1'b0}}, instruction[7:4]} : 16'bz;  // Controlled_Buffer controlled_buffer_5
  assign busA = UNNECESSARY_out ? {16{1'b0}} : 16'bz;  // Controlled_Buffer controlled_buffer_6
  or UNNECESSARY (UNNECESSARY_out, LI_out, J_out);
  assign bit_extender_1_out = {{4{instruction[15]}}, {instruction[15:14], instruction[3:2], instruction[11:4]}};  // Bit_Extender bit_extender_1
  assign bit_extender_2_out = {{7{instruction[3]}}, {instruction[3], instruction[11:4]}};  // Bit_Extender bit_extender_2
  assign busB = J_out ? bit_extender_1_out : 16'bz;  // Controlled_Buffer controlled_buffer_7
  assign busB = not_10_out ? {{12{1'b0}}, instruction[11:8]} : 16'bz;  // Controlled_Buffer controlled_buffer_8
  assign busB = I_out ? bit_extender_2_out : 16'bz;  // Controlled_Buffer controlled_buffer_9
  not not_10 (not_10_out, or_2_out);
  or or_2 (or_2_out, J_out, I_out);
  or can_simplify_with_b23 (can_simplify_with_b23_out, SI_out, I_out, J_out);
  not not_11 (regToA, LS_out);
  not not_12 (regToB, can_simplify_with_b23_out);
  not not_13 (not_13_out, instruction[2]);
  assign writebackDst = not_14_out ? instruction[15:12] : 4'bz;  // Controlled_Buffer controlled_buffer_10
  assign writebackDst = J_out ? {2'b00, instruction[13:12]} : 4'bz;  // Controlled_Buffer controlled_buffer_11
  not not_14 (not_14_out, or_3_out);
  assign writebackDst = or_4_out ? 4'b0000 : 4'bz;  // Controlled_Buffer controlled_buffer_12
  or or_3 (or_3_out, J_out, or_4_out);
  or or_4 (or_4_out, branch, memWrite);
  and and_6 (memWrite, not_13_out, LS_out);
  and and_7 (memRead, LS_out, instruction[2]);
  or or_5 (jump, JALR_out, J_out);

  // Notes on the sheet:
  //   NOTE: the "UNNECESSARY" gate can be replaced with direct output from "LI"
  //   It exists to prevent leaking undefined bits (though these bits would never get used)
endmodule

module RegisterFile (
  input  [3:0] selectA,
  input  [3:0] selectB,
  input  [3:0] selectWrite,
  input  [15:0] write,
  input  clock,
  input  reset,
  output [15:0] outputA,
  output [15:0] outputB
);

  wire and_1_out, and_2_out, and_3_out, and_4_out, and_5_out, and_6_out, and_7_out, and_8_out, and_9_out,
       and_10_out, and_11_out, and_12_out, and_13_out, and_14_out, and_15_out, and_16_out, and_17_out,
       and_18_out, and_19_out, and_20_out, and_21_out, and_22_out, and_23_out, and_24_out, and_25_out,
       and_26_out, and_27_out, and_28_out, and_29_out, and_30_out, and_31_out, and_32_out, and_33_out,
       and_34_out, and_35_out, and_36_out, and_37_out, and_38_out, and_39_out, and_40_out, and_41_out,
       and_42_out, and_43_out, and_44_out, and_45_out, and_46_out, and_47_out, and_48_out, and_49_out,
       and_50_out, and_51_out, and_52_out, decoder_1_out0, decoder_1_out1, decoder_1_out2, decoder_1_out3,
       decoder_2_out0, decoder_2_out1, decoder_2_out2, decoder_2_out3, decoder_3_out0, decoder_3_out1,
       decoder_3_out2, decoder_3_out3, decoder_4_out0, decoder_4_out1, decoder_4_out2, decoder_4_out3,
       decoder_5_out0, decoder_5_out1, decoder_5_out2, decoder_5_out3, decoder_6_out0, decoder_6_out1,
       decoder_6_out2, decoder_6_out3, not_1_out, not_2_out, or_1_out, or_2_out, or_3_out, undriven_2,
       undriven_3, undriven_4, undriven_5, undriven_6, undriven_7, undriven_8, undriven_9;
  wire [3:0] xor_1_out, xor_2_out;
  wire [15:0] controlled_buffer_1_out, controlled_buffer_2_out, controlled_buffer_3_out,
       controlled_buffer_7_out, register_1_q, register_2_q, register_3_q, register_4_q, register_5_q,
       register_6_q, register_7_q, register_8_q, register_9_q, register_10_q, register_11_q, register_12_q,
       register_13_q, register_14_q, register_15_q, register_16_q, undriven;

  Register #(.width(16)) register_1 (
    .D(undriven), .en(and_1_out), .clk(undriven_4), .Q(register_1_q), .clr(undriven_5));
  and and_1 (and_1_out, undriven_2, undriven_3);
  assign controlled_buffer_1_out = and_2_out ? register_1_q : 16'bz;  // Controlled_Buffer controlled_buffer_1
  and and_2 (and_2_out, undriven_9, undriven_6);
  Decoder #(.enable("false"), .select(2)) decoder_1 (
    .out0(decoder_1_out0), .out1(decoder_1_out1), .out2(decoder_1_out2), .out3(decoder_1_out3),
    .sel(selectA[3:2]));
  assign xor_1_out = selectA ^ selectWrite;  // XOR_Gate xor_1, 4 bits wide
  assign xor_2_out = selectB ^ selectWrite;  // XOR_Gate xor_2, 4 bits wide
  or or_1 (or_1_out, selectWrite[0], selectWrite[1], selectWrite[3], selectWrite[2]);
  assign controlled_buffer_2_out = and_3_out ? register_1_q : 16'bz;  // Controlled_Buffer controlled_buffer_2
  and and_3 (and_3_out, undriven_8, undriven_7);
  Decoder #(.enable("false"), .select(2)) decoder_2 (
    .out0(decoder_2_out0), .out1(decoder_2_out1), .out2(decoder_2_out2), .out3(decoder_2_out3),
    .sel(selectB[3:2]));
  or or_2 (or_2_out, xor_1_out[0], xor_1_out[1], xor_1_out[3], xor_1_out[2]);
  not not_1 (not_1_out, or_2_out);
  or or_3 (or_3_out, xor_2_out[0], xor_2_out[1], xor_2_out[3], xor_2_out[2]);
  not not_2 (not_2_out, or_3_out);
  Decoder #(.enable("false"), .select(2)) decoder_3 (
    .out0(decoder_3_out0), .out1(decoder_3_out1), .out2(decoder_3_out2), .out3(decoder_3_out3),
    .sel(selectA[1:0]));
  Decoder #(.enable("false"), .select(2)) decoder_4 (
    .out0(decoder_4_out0), .out1(decoder_4_out1), .out2(decoder_4_out2), .out3(decoder_4_out3),
    .sel(selectB[1:0]));
  Decoder #(.enable("false"), .select(2)) decoder_5 (
    .out0(decoder_5_out0), .out1(decoder_5_out1), .out2(decoder_5_out2), .out3(decoder_5_out3),
    .sel(selectWrite[1:0]));
  Decoder #(.enable("false"), .select(2)) decoder_6 (
    .out0(decoder_6_out0), .out1(decoder_6_out1), .out2(decoder_6_out2), .out3(decoder_6_out3),
    .sel(selectWrite[3:2]));
  and and_4 (and_4_out, not_1_out, or_1_out);
  and and_5 (and_5_out, not_2_out, or_1_out);
  Register #(.width(16)) register_2 (.D(write), .en(and_6_out), .clk(clock), .Q(register_2_q), .clr(reset));
  and and_6 (and_6_out, decoder_5_out3, decoder_6_out3);
  Register #(.width(16)) register_3 (.D(write), .en(and_7_out), .clk(clock), .Q(register_3_q), .clr(reset));
  and and_7 (and_7_out, decoder_5_out3, decoder_6_out2);
  Register #(.width(16)) register_4 (.D(write), .en(and_8_out), .clk(clock), .Q(register_4_q), .clr(reset));
  and and_8 (and_8_out, decoder_5_out3, decoder_6_out1);
  Register #(.width(16)) register_5 (.D(write), .en(and_9_out), .clk(clock), .Q(register_5_q), .clr(reset));
  and and_9 (and_9_out, decoder_5_out3, decoder_6_out0);
  assign controlled_buffer_3_out = and_10_out ? register_2_q : 16'bz;  // Controlled_Buffer controlled_buffer_3
  and and_10 (and_10_out, decoder_4_out3, decoder_2_out3);
  assign controlled_buffer_3_out = and_11_out ? register_3_q : 16'bz;  // Controlled_Buffer controlled_buffer_4
  and and_11 (and_11_out, decoder_4_out3, decoder_2_out2);
  assign controlled_buffer_3_out = and_12_out ? register_4_q : 16'bz;  // Controlled_Buffer controlled_buffer_5
  and and_12 (and_12_out, decoder_4_out3, decoder_2_out1);
  assign controlled_buffer_3_out = and_13_out ? register_5_q : 16'bz;  // Controlled_Buffer controlled_buffer_6
  and and_13 (and_13_out, decoder_4_out3, decoder_2_out0);
  assign controlled_buffer_7_out = and_14_out ? register_2_q : 16'bz;  // Controlled_Buffer controlled_buffer_7
  and and_14 (and_14_out, decoder_3_out3, decoder_1_out3);
  assign controlled_buffer_7_out = and_15_out ? register_3_q : 16'bz;  // Controlled_Buffer controlled_buffer_8
  and and_15 (and_15_out, decoder_3_out3, decoder_1_out2);
  assign controlled_buffer_7_out = and_16_out ? register_4_q : 16'bz;  // Controlled_Buffer controlled_buffer_9
  and and_16 (and_16_out, decoder_3_out3, decoder_1_out1);
  assign controlled_buffer_7_out = and_17_out ? register_5_q : 16'bz;  // Controlled_Buffer controlled_buffer_10
  and and_17 (and_17_out, decoder_3_out3, decoder_1_out0);
  Register #(.width(16)) register_6 (.D(write), .en(and_18_out), .clk(clock), .Q(register_6_q), .clr(reset));
  and and_18 (and_18_out, decoder_5_out2, decoder_6_out3);
  Register #(.width(16)) register_7 (.D(write), .en(and_19_out), .clk(clock), .Q(register_7_q), .clr(reset));
  and and_19 (and_19_out, decoder_5_out2, decoder_6_out2);
  Register #(.width(16)) register_8 (.D(write), .en(and_20_out), .clk(clock), .Q(register_8_q), .clr(reset));
  and and_20 (and_20_out, decoder_5_out2, decoder_6_out1);
  Register #(.width(16)) register_9 (.D(write), .en(and_21_out), .clk(clock), .Q(register_9_q), .clr(reset));
  and and_21 (and_21_out, decoder_5_out2, decoder_6_out0);
  assign controlled_buffer_3_out = and_22_out ? register_6_q : 16'bz;  // Controlled_Buffer controlled_buffer_11
  and and_22 (and_22_out, decoder_4_out2, decoder_2_out3);
  assign controlled_buffer_3_out = and_23_out ? register_7_q : 16'bz;  // Controlled_Buffer controlled_buffer_12
  and and_23 (and_23_out, decoder_4_out2, decoder_2_out2);
  assign controlled_buffer_3_out = and_24_out ? register_8_q : 16'bz;  // Controlled_Buffer controlled_buffer_13
  and and_24 (and_24_out, decoder_4_out2, decoder_2_out1);
  assign controlled_buffer_3_out = and_25_out ? register_9_q : 16'bz;  // Controlled_Buffer controlled_buffer_14
  and and_25 (and_25_out, decoder_4_out2, decoder_2_out0);
  assign controlled_buffer_7_out = and_26_out ? register_6_q : 16'bz;  // Controlled_Buffer controlled_buffer_15
  and and_26 (and_26_out, decoder_3_out2, decoder_1_out3);
  assign controlled_buffer_7_out = and_27_out ? register_7_q : 16'bz;  // Controlled_Buffer controlled_buffer_16
  and and_27 (and_27_out, decoder_3_out2, decoder_1_out2);
  assign controlled_buffer_7_out = and_28_out ? register_8_q : 16'bz;  // Controlled_Buffer controlled_buffer_17
  and and_28 (and_28_out, decoder_3_out2, decoder_1_out1);
  assign controlled_buffer_7_out = and_29_out ? register_9_q : 16'bz;  // Controlled_Buffer controlled_buffer_18
  and and_29 (and_29_out, decoder_3_out2, decoder_1_out0);
  Register #(.width(16)) register_10 (.D(write), .en(and_30_out), .clk(clock), .Q(register_10_q), .clr(reset));
  and and_30 (and_30_out, decoder_5_out1, decoder_6_out3);
  Register #(.width(16)) register_11 (.D(write), .en(and_31_out), .clk(clock), .Q(register_11_q), .clr(reset));
  and and_31 (and_31_out, decoder_5_out1, decoder_6_out2);
  Register #(.width(16)) register_12 (.D(write), .en(and_32_out), .clk(clock), .Q(register_12_q), .clr(reset));
  and and_32 (and_32_out, decoder_5_out1, decoder_6_out1);
  Register #(.width(16)) register_13 (.D(write), .en(and_33_out), .clk(clock), .Q(register_13_q), .clr(reset));
  and and_33 (and_33_out, decoder_5_out1, decoder_6_out0);
  assign controlled_buffer_3_out = and_34_out ? register_10_q : 16'bz;  // Controlled_Buffer controlled_buffer_19
  and and_34 (and_34_out, decoder_4_out1, decoder_2_out3);
  assign controlled_buffer_3_out = and_35_out ? register_11_q : 16'bz;  // Controlled_Buffer controlled_buffer_20
  and and_35 (and_35_out, decoder_4_out1, decoder_2_out2);
  assign controlled_buffer_3_out = and_36_out ? register_12_q : 16'bz;  // Controlled_Buffer controlled_buffer_21
  and and_36 (and_36_out, decoder_4_out1, decoder_2_out1);
  assign controlled_buffer_3_out = and_37_out ? register_13_q : 16'bz;  // Controlled_Buffer controlled_buffer_22
  and and_37 (and_37_out, decoder_4_out1, decoder_2_out0);
  assign controlled_buffer_7_out = and_38_out ? register_10_q : 16'bz;  // Controlled_Buffer controlled_buffer_23
  and and_38 (and_38_out, decoder_3_out1, decoder_1_out3);
  assign controlled_buffer_7_out = and_39_out ? register_11_q : 16'bz;  // Controlled_Buffer controlled_buffer_24
  and and_39 (and_39_out, decoder_3_out1, decoder_1_out2);
  assign controlled_buffer_7_out = and_40_out ? register_12_q : 16'bz;  // Controlled_Buffer controlled_buffer_25
  and and_40 (and_40_out, decoder_3_out1, decoder_1_out1);
  assign controlled_buffer_7_out = and_41_out ? register_13_q : 16'bz;  // Controlled_Buffer controlled_buffer_26
  and and_41 (and_41_out, decoder_3_out1, decoder_1_out0);
  Register #(.width(16)) register_14 (.D(write), .en(and_42_out), .clk(clock), .Q(register_14_q), .clr(reset));
  and and_42 (and_42_out, decoder_5_out0, decoder_6_out3);
  Register #(.width(16)) register_15 (.D(write), .en(and_43_out), .clk(clock), .Q(register_15_q), .clr(reset));
  and and_43 (and_43_out, decoder_5_out0, decoder_6_out2);
  Register #(.width(16)) register_16 (.D(write), .en(and_44_out), .clk(clock), .Q(register_16_q), .clr(reset));
  and and_44 (and_44_out, decoder_5_out0, decoder_6_out1);
  assign controlled_buffer_3_out = and_45_out ? register_14_q : 16'bz;  // Controlled_Buffer controlled_buffer_27
  and and_45 (and_45_out, decoder_4_out0, decoder_2_out3);
  assign controlled_buffer_3_out = and_46_out ? register_15_q : 16'bz;  // Controlled_Buffer controlled_buffer_28
  and and_46 (and_46_out, decoder_4_out0, decoder_2_out2);
  assign controlled_buffer_3_out = and_47_out ? register_16_q : 16'bz;  // Controlled_Buffer controlled_buffer_29
  and and_47 (and_47_out, decoder_4_out0, decoder_2_out1);
  assign controlled_buffer_3_out = and_48_out ? {16{1'b0}} : 16'bz;  // Controlled_Buffer controlled_buffer_30
  and and_48 (and_48_out, decoder_4_out0, decoder_2_out0);
  assign controlled_buffer_7_out = and_49_out ? register_14_q : 16'bz;  // Controlled_Buffer controlled_buffer_31
  and and_49 (and_49_out, decoder_3_out0, decoder_1_out3);
  assign controlled_buffer_7_out = and_50_out ? register_15_q : 16'bz;  // Controlled_Buffer controlled_buffer_32
  and and_50 (and_50_out, decoder_3_out0, decoder_1_out2);
  assign controlled_buffer_7_out = and_51_out ? register_16_q : 16'bz;  // Controlled_Buffer controlled_buffer_33
  and and_51 (and_51_out, decoder_3_out0, decoder_1_out1);
  assign controlled_buffer_7_out = and_52_out ? {16{1'b0}} : 16'bz;  // Controlled_Buffer controlled_buffer_34
  and and_52 (and_52_out, decoder_3_out0, decoder_1_out0);
  Multiplexer #(.width(16)) multiplexer_1 (.in0(controlled_buffer_7_out), .in1(write), .out(outputA), .sel(and_4_out));
  Multiplexer #(.width(16)) multiplexer_2 (.in0(controlled_buffer_3_out), .in1(write), .out(outputB), .sel(and_5_out));

  // Notes on the sheet:
  //   unit
endmodule

module ALU (
  input  [15:0] A,
  input  [15:0] B,
  input  [3:0] operation,
  output [15:0] result,
  output zero
);

  wire adder_1_cout, and_2_out, and_3_out, comparator_1_eq, comparator_1_gt, comparator_1_lt,
       comparator_2_eq, comparator_2_gt, comparator_2_lt, not_1_out, not_2_out, xor_2_out;
  wire [0:0] multiplexer_2_out;
  wire [15:0] adder_1_out, and_1_out, divider_1_out, divider_1_rem, multiplexer_1_out, multiplexer_3_out,
       multiplexer_4_out, multiplier_1_cout, multiplier_1_out, negator_1_out, or_1_out, shifter_1_out,
       shifter_2_out, shifter_3_out, xor_1_out;

  Multiplexer #(.width(16)) multiplexer_1 (.in0(B), .in1(negator_1_out), .out(multiplexer_1_out), .sel(operation[0]));
  Negator #(.width(16)) negator_1 (.in(B), .out(negator_1_out));
  Adder #(.width(16)) adder_1 (.a(A), .b(multiplexer_1_out), .out(adder_1_out), .cin(1'b0), .cout(adder_1_cout));
  // NoConnect on adder_1_cout
  // NoConnect on comparator_1_gt
  // NoConnect on comparator_1_eq
  Comparator #(.width(16)) comparator_1 (
    .a(A), .b(B), .gt(comparator_1_gt), .eq(comparator_1_eq), .lt(comparator_1_lt));
  // NoConnect on comparator_2_gt
  // NoConnect on comparator_2_eq
  Comparator #(.mode("unsigned"), .width(16)) comparator_2 (
    .a(A), .b(B), .gt(comparator_2_gt), .eq(comparator_2_eq), .lt(comparator_2_lt));
  Divider #(.width(16)) divider_1 (.a(A), .b(B), .out(divider_1_out), .upper({16{1'b0}}), .rem(divider_1_rem));
  // NoConnect on divider_1_rem
  Shifter #(.width(16)) shifter_1 (.in(A), .\dist (B[3:0]), .out(shifter_1_out));
  Shifter #(.shift("ar"), .width(16)) shifter_2 (.in(A), .\dist (B[3:0]), .out(shifter_2_out));
  Shifter #(.shift("lr"), .width(16)) shifter_3 (.in(A), .\dist (B[3:0]), .out(shifter_3_out));
  assign xor_1_out = A ^ B;  // XOR_Gate xor_1, 16 bits wide
  assign or_1_out = A | B;  // OR_Gate or_1, 16 bits wide
  assign and_1_out = A & B;  // AND_Gate and_1, 16 bits wide
  Multiplier #(.width(16)) multiplier_1 (
    .a(A), .b(B), .out(multiplier_1_out), .cin({16{1'b0}}), .cout(multiplier_1_cout));
  Multiplexer multiplexer_2 (
    .in0(comparator_1_lt), .in1(comparator_2_lt), .out(multiplexer_2_out[0]), .sel(operation[0]));
  Multiplexer #(.select(3), .width(16)) multiplexer_3 (
    .in0(shifter_1_out), .in1(shifter_2_out), .in2(shifter_3_out), .in3(xor_1_out), .in4(or_1_out),
    .in5(and_1_out), .in6(multiplier_1_out), .in7(multiplier_1_cout), .out(multiplexer_3_out),
    .sel(operation[2:0]));
  assign result = and_2_out ? multiplexer_4_out : 16'bz;  // Controlled_Buffer controlled_buffer_1
  Multiplexer #(.width(16)) multiplexer_4 (
    .in0(adder_1_out), .in1({{15{1'b0}}, multiplexer_2_out[0]}), .out(multiplexer_4_out), .sel(operation[1]));
  not not_1 (not_1_out, operation[2]);
  not not_2 (not_2_out, operation[3]);
  assign result = and_3_out ? divider_1_out : 16'bz;  // Controlled_Buffer controlled_buffer_2
  assign result = operation[3] ? multiplexer_3_out : 16'bz;  // Controlled_Buffer controlled_buffer_3
  and and_2 (and_2_out, not_1_out, not_2_out);
  and and_3 (and_3_out, operation[2], not_2_out);
  ExactlyOne xor_2 (
    .out(xor_2_out), .in0(result[0]), .in1(result[1]), .in2(result[2]), .in3(result[3]), .in4(result[4]),
    .in5(result[5]), .in6(result[6]), .in7(result[7]), .in8(result[9]), .in9(result[10]), .in10(result[11]),
    .in11(result[12]), .in12(result[13]), .in13(result[14]), .in14(result[15]), .in15(result[8]));
  not not_3 (zero, xor_2_out);
endmodule

module ID_EX_PSB (
  input  [15:0] ibusA,
  input  [15:0] ibusB,
  input  [3:0] ialuOp,
  input  imemRead,
  input  imemWrite,
  input  [15:0] imemWriteVal,
  input  [15:0] inextPC,
  input  [15:0] ijumpPC,
  input  ijump,
  input  ibranch,
  input  ibranchType,
  input  [3:0] iwritebackDst,
  input  [3:0] iregA,
  input  iregToA,
  input  [3:0] iregB,
  input  iregToB,
  input  [3:0] imemWriteReg,
  input  writeEnable,
  input  clock,
  input  reset,
  output [15:0] busA,
  output [15:0] busB,
  output [3:0] aluOp,
  output memRead,
  output memWrite,
  output [15:0] memWriteVal,
  output [15:0] nextPC,
  output [15:0] jumpPC,
  output jump,
  output branch,
  output branchType,
  output [3:0] writebackDst,
  output [3:0] regA,
  output regToA,
  output [3:0] regB,
  output regToB,
  output [3:0] memWriteReg
);

  Register #(.width(16)) register_1 (.D(ibusA), .en(writeEnable), .clk(clock), .Q(busA), .clr(reset));
  Register #(.width(16)) register_2 (.D(ibusB), .en(writeEnable), .clk(clock), .Q(busB), .clr(reset));
  Register #(.width(4)) register_3 (.D(ialuOp), .en(writeEnable), .clk(clock), .Q(aluOp), .clr(reset));
  Register #(.width(1)) register_4 (.D(imemRead), .en(writeEnable), .clk(clock), .Q(memRead), .clr(reset));
  Register #(.width(1)) register_5 (.D(imemWrite), .en(writeEnable), .clk(clock), .Q(memWrite), .clr(reset));
  Register #(.width(16)) register_6 (.D(imemWriteVal), .en(writeEnable), .clk(clock), .Q(memWriteVal), .clr(reset));
  Register #(.width(16)) register_7 (.D(inextPC), .en(writeEnable), .clk(clock), .Q(nextPC), .clr(reset));
  Register #(.width(16)) register_8 (.D(ijumpPC), .en(writeEnable), .clk(clock), .Q(jumpPC), .clr(reset));
  Register #(.width(1)) register_9 (.D(ijump), .en(writeEnable), .clk(clock), .Q(jump), .clr(reset));
  Register #(.width(1)) register_10 (.D(ibranch), .en(writeEnable), .clk(clock), .Q(branch), .clr(reset));
  Register #(.width(1)) register_11 (.D(ibranchType), .en(writeEnable), .clk(clock), .Q(branchType), .clr(reset));
  Register #(.width(4)) register_12 (.D(iwritebackDst), .en(writeEnable), .clk(clock), .Q(writebackDst), .clr(reset));
  Register #(.width(4)) register_13 (.D(iregA), .en(writeEnable), .clk(clock), .Q(regA), .clr(reset));
  Register #(.width(1)) register_14 (.D(iregToA), .en(writeEnable), .clk(clock), .Q(regToA), .clr(reset));
  Register #(.width(4)) register_15 (.D(iregB), .en(writeEnable), .clk(clock), .Q(regB), .clr(reset));
  Register #(.width(1)) register_16 (.D(iregToB), .en(writeEnable), .clk(clock), .Q(regToB), .clr(reset));
  Register #(.width(4)) register_17 (.D(imemWriteReg), .en(writeEnable), .clk(clock), .Q(memWriteReg), .clr(reset));
endmodule

module EX_ME_PSB (
  input  [15:0] iwritebackVal,
  input  [15:0] ialuResult,
  input  imemRead,
  input  imemWrite,
  input  [15:0] imemWriteVal,
  input  [3:0] iwritebackDst,
  input  writeEnable,
  input  clock,
  input  reset,
  output [15:0] writebackVal,
  output [15:0] aluResult,
  output memRead,
  output memWrite,
  output [15:0] memWriteVal,
  output [3:0] writebackDst
);

  Register #(.width(16)) register_1 (.D(iwritebackVal), .en(writeEnable), .clk(clock), .Q(writebackVal), .clr(reset));
  Register #(.width(16)) register_2 (.D(ialuResult), .en(writeEnable), .clk(clock), .Q(aluResult), .clr(reset));
  Register #(.width(1)) register_3 (.D(imemRead), .en(writeEnable), .clk(clock), .Q(memRead), .clr(reset));
  Register #(.width(1)) register_4 (.D(imemWrite), .en(writeEnable), .clk(clock), .Q(memWrite), .clr(reset));
  Register #(.width(16)) register_5 (.D(imemWriteVal), .en(writeEnable), .clk(clock), .Q(memWriteVal), .clr(reset));
  Register #(.width(4)) register_6 (.D(iwritebackDst), .en(writeEnable), .clk(clock), .Q(writebackDst), .clr(reset));
endmodule

module IF_ID_PSB (
  input  [15:0] inextPC,
  input  [15:0] iinstruction,
  input  writeEnable,
  input  clock,
  input  reset,
  output [15:0] nextPC,
  output [15:0] instruction
);

  Register #(.width(16)) register_1 (.D(inextPC), .en(writeEnable), .clk(clock), .Q(nextPC), .clr(reset));
  Register #(.width(16)) register_2 (.D(iinstruction), .en(writeEnable), .clk(clock), .Q(instruction), .clr(reset));
endmodule

module ME_WB_PSB (
  input  [15:0] iwritebackVal,
  input  [15:0] imemReadVal,
  input  imemRead,
  input  [3:0] iwritebackDst,
  input  writeEnable,
  input  clock,
  input  reset,
  output [15:0] writebackVal,
  output [15:0] memReadVal,
  output memRead,
  output [3:0] writebackDst
);

  Register #(.width(16)) register_1 (.D(iwritebackVal), .en(writeEnable), .clk(clock), .Q(writebackVal), .clr(reset));
  Register #(.width(16)) register_2 (.D(imemReadVal), .en(writeEnable), .clk(clock), .Q(memReadVal), .clr(reset));
  Register #(.width(1)) register_3 (.D(imemRead), .en(writeEnable), .clk(clock), .Q(memRead), .clr(reset));
  Register #(.width(4)) register_4 (.D(iwritebackDst), .en(writeEnable), .clk(clock), .Q(writebackDst), .clr(reset));
endmodule

module ForwardUnit (
  input  [3:0] MEdst,
  input  [3:0] WBdst,
  input  [3:0] r1,
  input  r1a,
  input  [3:0] r2,
  input  r2a,
  input  [3:0] rStore,
  input  rStorea,
  output aFromME,
  output aFromWB,
  output bFromME,
  output bFromWB,
  output storeFromME,
  output storeFromWB
);

  wire and_1_out, and_2_out, and_3_out, not_1_out, not_2_out, not_3_out, not_4_out, not_5_out, not_6_out,
       or_1_out, or_2_out, or_3_out, or_4_out, or_5_out, or_6_out, or_7_out, or_8_out, or_9_out;
  wire [3:0] xor_1_out, xor_2_out, xor_3_out, xor_4_out, xor_5_out, xor_6_out;

  or or_1 (or_1_out, r1[0], r1[1], r1[3], r1[2]);
  or or_2 (or_2_out, r2[0], r2[1], r2[3], r2[2]);
  or or_3 (or_3_out, rStore[0], rStore[1], rStore[3], rStore[2]);
  and and_1 (and_1_out, or_1_out, r1a);
  and and_2 (and_2_out, or_2_out, r2a);
  and and_3 (and_3_out, or_3_out, rStorea);
  assign xor_1_out = MEdst ^ r1;  // XOR_Gate xor_1, 4 bits wide
  assign xor_2_out = WBdst ^ r1;  // XOR_Gate xor_2, 4 bits wide
  assign xor_3_out = MEdst ^ r2;  // XOR_Gate xor_3, 4 bits wide
  assign xor_4_out = WBdst ^ r2;  // XOR_Gate xor_4, 4 bits wide
  assign xor_5_out = MEdst ^ rStore;  // XOR_Gate xor_5, 4 bits wide
  assign xor_6_out = WBdst ^ rStore;  // XOR_Gate xor_6, 4 bits wide
  or or_4 (or_4_out, xor_1_out[0], xor_1_out[1], xor_1_out[3], xor_1_out[2]);
  not not_1 (not_1_out, or_4_out);
  or or_5 (or_5_out, xor_2_out[0], xor_2_out[1], xor_2_out[3], xor_2_out[2]);
  not not_2 (not_2_out, or_5_out);
  or or_6 (or_6_out, xor_3_out[0], xor_3_out[1], xor_3_out[3], xor_3_out[2]);
  not not_3 (not_3_out, or_6_out);
  or or_7 (or_7_out, xor_4_out[0], xor_4_out[1], xor_4_out[3], xor_4_out[2]);
  not not_4 (not_4_out, or_7_out);
  or or_8 (or_8_out, xor_5_out[0], xor_5_out[1], xor_5_out[3], xor_5_out[2]);
  not not_5 (not_5_out, or_8_out);
  or or_9 (or_9_out, xor_6_out[0], xor_6_out[1], xor_6_out[3], xor_6_out[2]);
  not not_6 (not_6_out, or_9_out);
  and and_4 (aFromME, not_1_out, and_1_out);
  and and_5 (aFromWB, not_2_out, and_1_out);
  and and_6 (bFromME, not_3_out, and_2_out);
  and and_7 (bFromWB, not_4_out, and_2_out);
  and and_8 (storeFromME, not_5_out, and_3_out);
  and and_9 (storeFromWB, not_6_out, and_3_out);
endmodule

module HazardDetector (
  input  [3:0] EXwritebackDst,
  input  EXmemRead,
  input  [3:0] IDregA,
  input  IDregToA,
  input  [3:0] IDregB,
  input  IDregToB,
  output stall
);

  wire and_1_out, and_2_out, not_1_out, not_2_out, or_1_out, or_2_out, or_3_out, or_4_out;
  wire [3:0] xor_1_out, xor_2_out;

  or or_1 (or_1_out, EXwritebackDst[0], EXwritebackDst[1], EXwritebackDst[3], EXwritebackDst[2]);
  assign xor_1_out = EXwritebackDst ^ IDregA;  // XOR_Gate xor_1, 4 bits wide
  assign xor_2_out = EXwritebackDst ^ IDregB;  // XOR_Gate xor_2, 4 bits wide
  or or_2 (or_2_out, xor_1_out[0], xor_1_out[1], xor_1_out[3], xor_1_out[2]);
  not not_1 (not_1_out, or_2_out);
  or or_3 (or_3_out, xor_2_out[0], xor_2_out[1], xor_2_out[3], xor_2_out[2]);
  not not_2 (not_2_out, or_3_out);
  and and_1 (and_1_out, not_1_out, IDregToA);
  or or_4 (or_4_out, and_1_out, and_2_out);
  and and_2 (and_2_out, not_2_out, IDregToB);
  and and_3 (stall, or_1_out, or_4_out, EXmemRead);

  // Notes on the sheet:
  //   stall = (EX.memRead && EX.writebackDst != 0 && ((ID.regToA && ID.regA == EX.writebackDst) || (ID.regToB && ID.regB == EX.writebackDst)))
endmodule
